// Logisim project Adder_Subtractor_8bit.circ as structural Verilog: 4 circuits, main circuit FullAdder
module FullAdder (
  input  C_in,
  input  A,
  input  B,
  output out_4,
  output Q
);

  wire nor_1_out, nor_2_out, nor_3_out, nor_4_out, nor_5_out, nor_7_out, nor_8_out;

  nor nor_1 (nor_1_out, A, B);
  nor nor_2 (nor_2_out, A, nor_1_out);
  nor nor_3 (nor_3_out, nor_1_out, B);
  nor nor_4 (nor_4_out, nor_2_out, nor_3_out);
  nor nor_5 (nor_5_out, C_in, nor_4_out);
  nor nor_6 (out_4, nor_1_out, nor_5_out);
  nor nor_7 (nor_7_out, C_in, nor_5_out);
  nor nor_8 (nor_8_out, nor_5_out, nor_4_out);
  nor nor_9 (Q, nor_7_out, nor_8_out);
endmodule

module Adder8bit (
  input  C_in,
  input  [7:0] A,
  input  [7:0] B,
  output [7:0] Q,
  output C_out
);

  wire fulladder_1_out_4, fulladder_2_out_4, fulladder_3_out_4, fulladder_4_out_4, fulladder_5_out_4,
       fulladder_6_out_4, fulladder_7_out_4;

  FullAdder fulladder_1 (.out_4(fulladder_1_out_4), .Q(Q[0]), .C_in(C_in), .A(A[0]), .B(B[0]));
  FullAdder fulladder_2 (.out_4(fulladder_2_out_4), .Q(Q[1]), .C_in(fulladder_1_out_4), .A(A[1]), .B(B[1]));
  FullAdder fulladder_3 (.out_4(fulladder_3_out_4), .Q(Q[2]), .C_in(fulladder_2_out_4), .A(A[2]), .B(B[2]));
  FullAdder fulladder_4 (.out_4(fulladder_4_out_4), .Q(Q[3]), .C_in(fulladder_3_out_4), .A(A[3]), .B(B[3]));
  FullAdder fulladder_5 (.out_4(fulladder_5_out_4), .Q(Q[4]), .C_in(fulladder_4_out_4), .A(A[4]), .B(B[4]));
  FullAdder fulladder_6 (.out_4(fulladder_6_out_4), .Q(Q[5]), .C_in(fulladder_5_out_4), .A(A[5]), .B(B[5]));
  FullAdder fulladder_7 (.out_4(fulladder_7_out_4), .Q(Q[6]), .C_in(fulladder_6_out_4), .A(A[6]), .B(B[6]));
  FullAdder fulladder_8 (.out_4(C_out), .Q(Q[7]), .C_in(fulladder_7_out_4), .A(A[7]), .B(B[7]));

  // Notes on the sheet:
  //   Putting a 1 on the carry input is the same as adding one overall for 2's compliment
endmodule

module ModeControl (
  input  Subtract,
  input  [7:0] In,
  output Carry_out,
  output [7:0] Out
);

  wire [7:7] not_1_out;

  not not_1 (not_1_out[7], Subtract);
  assign Out = ~(In ^ {8{not_1_out[7]}});  // XNOR_Gate xnor_1, 8 bits wide

  assign Carry_out = Subtract;
endmodule

module AdderSubtracter (
  input  [7:0] A,
  input  Sub,
  input  [7:0] B,
  output [7:0] Q,
  output C_out
);

  wire modecontrol_1_carry_out;
  wire [7:0] modecontrol_1_out;

  ModeControl modecontrol_1 (.Carry_out(modecontrol_1_carry_out), .Out(modecontrol_1_out), .Subtract(Sub), .In(B));
  Adder8bit adder8bit_1 (.Q(Q), .C_out(C_out), .A(A), .B(modecontrol_1_out), .C_in(modecontrol_1_carry_out));
endmodule
