// Logisim project Computer.circ as structural Verilog: 1 circuit, main circuit DataPath
module DataPath (
  input  OpWriteEn,
  input  [3:0] in_2,
  input  OwriteEn,
  input  Clr
);

  wire and_1_out, and_2_out, Awrite_out, Bwrite_out, Clk_out, instrdecode_1_one, instrdecode_1_out_4,
       instrdecode_1_out_5, instrdecode_1_out_6, instrdecode_1_out_7, instrdecode_1_out_8,
       instrdecode_1_out_9, instrdecode_1_out_10, instrdecode_1_out_11, instrdecode_1_out_12,
       instrdecode_1_out_13, instrdecode_1_out_14, instrdecode_1_out_15, instrdecode_1_out_16,
       instrdecode_1_out_17, instrdecode_1_out_18, logicunit_1_out_2, logicunit_1_out_3, MemAcc_out,
       MemWri_out, multiplexer_1_out, or_1_out, or_2_out, or_3_out, or_4_out, or_5_out, or_6_out, or_7_out,
       or_10_out, or_13_out, or_14_out, or_15_out, or_16_out, or_17_out, or_18_out, or_19_out, or_20_out,
       phase_1_p1, phase_1_p2, phase_1_p3;
  wire [1:0] or_8_out, or_11_out;
  wire [3:0] main_1_out_6, O_Reg_out_5, O_Reg_out_5_2, undriven;
  wire [7:0] A_Reg_out_5, adder8bit_1_q, adder8bit_2_q, adder8bit_3_q, B_Reg_out_5, main_1_out_6_2,
       multiplexer_2_out, multiplexer_3_out, multiplexer_4_out, multiplexer_5_out, multiplexer_6_out,
       multiplexer_7_out, not_1_out, not_2_out, Opcode_out_5, PC_Reg_out_5;

  or or_1 (or_1_out, phase_1_p2, and_1_out);
  and and_1 (and_1_out, phase_1_p3, or_2_out);
  or or_2 (or_2_out, or_3_out, and_2_out);
  LogicUnit logicunit_1 (.out_3(logicunit_1_out_3), .out_2(logicunit_1_out_2), .in_1(adder8bit_1_q));
  Adder8bit adder8bit_1 (.Q(adder8bit_1_q), .A({8{1'b0}}), .B(not_1_out), .C_in(1'b1));  // open: C_out
  or or_3 (or_3_out, instrdecode_1_out_12, instrdecode_1_out_15);
  and and_2 (and_2_out, multiplexer_1_out, or_4_out);
  or or_4 (or_4_out, instrdecode_1_out_13, instrdecode_1_out_14);
  Multiplexer #(.enable("false")) multiplexer_1 (
    .in0(logicunit_1_out_2), .in1(logicunit_1_out_3), .out(multiplexer_1_out), .sel(or_5_out));
  buf or_5 (or_5_out, instrdecode_1_out_14);  // OR_Gate
  assign not_1_out = ~A_Reg_out_5;  // NOT_Gate not_1, 8 bits wide
  Register8bit Opcode (.out_5(Opcode_out_5), .in_4({main_1_out_6, undriven}), .Clk(Clk_out), .En(OpWriteEn), .Clr(Clr));
  Main main_1 (
    .out_6({main_1_out_6, main_1_out_6_2[3:0]}), .W(MemWri_out), .in_5(A_Reg_out_5),
    .Address(multiplexer_2_out), .Clr(Clr), .Clk(Clk_out));
  Multiplexer #(.enable("false"), .width(8)) multiplexer_2 (
    .in0(PC_Reg_out_5), .in1(adder8bit_2_q), .out(multiplexer_2_out), .sel(MemAcc_out));
  Multiplexer #(.enable("false"), .width(8)) multiplexer_3 (
    .in0(adder8bit_2_q), .in1({main_1_out_6, main_1_out_6_2[3:0]}), .out(multiplexer_3_out), .sel(MemAcc_out));
  Adder8bit adder8bit_2 (
    .Q(adder8bit_2_q), .A(multiplexer_5_out), .B(multiplexer_4_out), .C_in(or_7_out));  // open: C_out
  Multiplexer #(.enable("false"), .width(8)) multiplexer_4 (
    .in0(multiplexer_6_out), .in1(not_2_out), .out(multiplexer_4_out), .sel(or_7_out));
  assign not_2_out = ~multiplexer_6_out;  // NOT_Gate not_2, 8 bits wide
  Multiplexer #(.enable("false"), .select(2), .width(8)) multiplexer_5 (
    .in0(A_Reg_out_5), .in1(PC_Reg_out_5), .in2({O_Reg_out_5_2, O_Reg_out_5}), .in3({8{1'b0}}),
    .out(multiplexer_5_out), .sel(or_11_out));
  Register8bit A_Reg (.out_5(A_Reg_out_5), .in_4(multiplexer_3_out), .Clk(Clk_out), .En(Awrite_out), .Clr(Clr));
  and Awrite (Awrite_out, phase_1_p3, or_17_out);
  and Bwrite (Bwrite_out, phase_1_p3, or_18_out);
  and MemWri (MemWri_out, phase_1_p3, or_19_out);
  and MemAcc (MemAcc_out, phase_1_p3, or_6_out);
  Multiplexer #(.enable("false"), .select(2), .width(8)) multiplexer_6 (
    .in0(B_Reg_out_5), .in2({O_Reg_out_5_2, O_Reg_out_5}), .in3({8{1'b0}}), .out(multiplexer_6_out),
    .sel(or_8_out));  // open: in1
  Register8bit B_Reg (.out_5(B_Reg_out_5), .in_4(multiplexer_3_out), .Clk(Clk_out), .En(Bwrite_out), .Clr(Clr));
  or or_6 (or_6_out, or_19_out, or_20_out);
  buf or_7 (or_7_out, instrdecode_1_out_17);  // OR_Gate
  buf or_8 (or_8_out[0], or_14_out);  // OR_Gate
  or or_9 (or_8_out[1], or_13_out, or_14_out);
  or or_10 (or_10_out, instrdecode_1_out_14, instrdecode_1_out_13, instrdecode_1_out_12, instrdecode_1_out_8);
  or or_11 (or_11_out[0], or_10_out, or_15_out);
  or or_12 (or_11_out[1], or_15_out, or_16_out);
  or or_13 (or_13_out, instrdecode_1_out_14, instrdecode_1_out_13, instrdecode_1_out_12, instrdecode_1_out_9, instrdecode_1_out_8);
  or or_14 (or_14_out, instrdecode_1_out_7, instrdecode_1_out_6, instrdecode_1_out_5, instrdecode_1_one);
  or or_15 (or_15_out, instrdecode_1_out_15, instrdecode_1_out_4);
  or or_16 (or_16_out, instrdecode_1_out_11, instrdecode_1_out_10, instrdecode_1_out_7, instrdecode_1_out_6, instrdecode_1_out_5, instrdecode_1_out_4, instrdecode_1_one);
  Register8bit PC_Reg (.out_5(PC_Reg_out_5), .in_4(multiplexer_7_out), .Clk(Clk_out), .En(or_1_out), .Clr(Clr));
  Multiplexer #(.enable("false"), .width(8)) multiplexer_7 (
    .in0(adder8bit_3_q), .in1(multiplexer_3_out), .out(multiplexer_7_out), .sel(or_1_out));
  Adder8bit adder8bit_3 (.Q(adder8bit_3_q), .A(PC_Reg_out_5), .B(8'h1));  // open: C_out, C_in
  or or_17 (or_17_out, instrdecode_1_out_17, instrdecode_1_out_16, instrdecode_1_out_9, instrdecode_1_out_8, instrdecode_1_out_6, instrdecode_1_one);
  or or_18 (or_18_out, instrdecode_1_out_10, instrdecode_1_out_7, instrdecode_1_out_4);
  or or_19 (or_19_out, instrdecode_1_out_11, instrdecode_1_out_5);
  or or_20 (or_20_out, instrdecode_1_out_10, instrdecode_1_out_9, instrdecode_1_out_4, instrdecode_1_one);
  Register8bit O_Reg (
    .out_5({O_Reg_out_5_2, O_Reg_out_5}), .in_4(main_1_out_6_2), .Clk(Clk_out), .En(OwriteEn), .Clr(Clr));
  Multiplexer #(.enable("false"), .width(4)) multiplexer_8 (
    .in1(O_Reg_out_5), .out(main_1_out_6_2[7:4]), .sel(instrdecode_1_out_18));  // open: in0
  InstrDecode instrdecode_1 (
    .out_6(instrdecode_1_out_6), .out_7(instrdecode_1_out_7), .out_8(instrdecode_1_out_8),
    .out_9(instrdecode_1_out_9), .out_10(instrdecode_1_out_10), .out_11(instrdecode_1_out_11),
    .out_12(instrdecode_1_out_12), .out_13(instrdecode_1_out_13), .out_14(instrdecode_1_out_14),
    .out_15(instrdecode_1_out_15), .out_16(instrdecode_1_out_16), .out_17(instrdecode_1_out_17),
    .out_18(instrdecode_1_out_18), .One(instrdecode_1_one), .out_4(instrdecode_1_out_4),
    .out_5(instrdecode_1_out_5), .OnOff(phase_1_p1), .Instruction(in_2));
  Phase phase_1 (.P1(phase_1_p1), .P2(phase_1_p2), .P3(phase_1_p3), .Clk(Clk_out), .Clr(Clr));
  Clock Clk (.out(Clk_out));

  // Notes on the sheet:
  //   Phase2
  //   UncondBranch
  //   CondBranch
  //   Cpmarison
  //   Phase 3
  //   AwriteEn
  //   BwriteEn
  //   MemWrite
  //   MemAccess
  //   O-mode
  //   0: lower  1: upper
  //   0to15
endmodule
