// Logisim project Computer3.circ as structural Verilog: 1 circuit, main circuit DataPath
module DataPath (
  input  in_1,
  input  [3:0] in_2,
  input  Clr,
  output [3:0] out_4,
  output [3:0] out_5,
  output [7:0] A,
  output [7:0] B,
  output [7:0] PC,
  output [7:0] O
);

  wire and_1_out, and_2_out, and_3_out, Awrite_out, Bwrite_out, Clk_out, instrdecode_1_one,
       instrdecode_1_out_4, instrdecode_1_out_5, instrdecode_1_out_6, instrdecode_1_out_7,
       instrdecode_1_out_8, instrdecode_1_out_9, instrdecode_1_out_10, instrdecode_1_out_11,
       instrdecode_1_out_12, instrdecode_1_out_13, instrdecode_1_out_14, instrdecode_1_out_15,
       instrdecode_1_out_16, instrdecode_1_out_17, instrdecode_1_out_18, logicunit_1_out_2,
       logicunit_1_out_3, MemAcc_out, MemWri_out, multiplexer_1_out, or_1_out, or_2_out, or_3_out, or_4_out,
       or_5_out, or_8_out, or_9_out, or_10_out, or_11_out, or_14_out, or_15_out, or_16_out, or_17_out,
       or_18_out, or_19_out, or_20_out, phase_1_p1, phase_1_p2, phase_1_p3;
  wire [1:0] or_6_out, or_12_out;
  wire [3:0] multiplexer_9_out, ram_1_dout, ram_1_dout_2, register8bit_1_out_5, undriven;
  wire [7:0] adder8bit_1_q, adder8bit_2_q, adder8bit_3_q, multiplexer_2_out, multiplexer_3_out,
       multiplexer_4_out, multiplexer_5_out, multiplexer_6_out, multiplexer_7_out, multiplexer_8_out,
       not_1_out, not_2_out;

  or or_1 (or_1_out, phase_1_p2, and_1_out);
  and and_1 (and_1_out, phase_1_p3, or_3_out);
  or or_2 (or_2_out, instrdecode_1_out_12, instrdecode_1_out_15);
  or or_3 (or_3_out, or_2_out, and_2_out);
  and and_2 (and_2_out, multiplexer_1_out, or_4_out);
  Multiplexer #(.enable("false")) multiplexer_1 (
    .in0(logicunit_1_out_2), .in1(logicunit_1_out_3), .out(multiplexer_1_out), .sel(instrdecode_1_out_14));
  LogicUnit logicunit_1 (.out_3(logicunit_1_out_3), .out_2(logicunit_1_out_2), .in_1(adder8bit_1_q));
  Adder8bit adder8bit_1 (.Q(adder8bit_1_q), .A({8{1'b0}}), .B(not_1_out), .C_in(1'b1));  // open: C_out
  or or_4 (or_4_out, instrdecode_1_out_13, instrdecode_1_out_14);
  assign not_1_out = ~A;  // NOT_Gate not_1, 8 bits wide
  Register8bit register8bit_1 (
    .out_5({out_4, register8bit_1_out_5}), .in_4({ram_1_dout, undriven}), .Clk(Clk_out), .En(phase_1_p1),
    .Clr(Clr));
  RAM #(.asyncread("true")) ram_1 (
    .addr(multiplexer_2_out), .we(MemWri_out), .oe(1'b1), .clk(Clk_out), .din(A),
    .dout({ram_1_dout, ram_1_dout_2}));
  Multiplexer #(.enable("false"), .width(8)) multiplexer_2 (
    .in0(PC), .in1(adder8bit_2_q), .out(multiplexer_2_out), .sel(MemAcc_out));
  Adder8bit adder8bit_2 (
    .Q(adder8bit_2_q), .A(multiplexer_5_out), .B(multiplexer_4_out), .C_in(or_5_out));  // open: C_out
  Register8bit register8bit_2 (.out_5(A), .in_4(multiplexer_3_out), .Clk(Clk_out), .En(Awrite_out), .Clr(Clr));
  Multiplexer #(.enable("false"), .width(8)) multiplexer_3 (
    .in0(adder8bit_2_q), .in1({ram_1_dout, ram_1_dout_2}), .out(multiplexer_3_out), .sel(MemAcc_out));
  Multiplexer #(.enable("false"), .width(8)) multiplexer_4 (
    .in0(multiplexer_6_out), .in1(not_2_out), .out(multiplexer_4_out), .sel(or_5_out));
  assign not_2_out = ~multiplexer_6_out;  // NOT_Gate not_2, 8 bits wide
  Multiplexer #(.enable("false"), .select(2), .width(8)) multiplexer_5 (
    .in0(A), .in1(PC), .in2(O), .in3({8{1'b0}}), .out(multiplexer_5_out), .sel(or_12_out));
  and Awrite (Awrite_out, phase_1_p3, or_16_out);
  and Bwrite (Bwrite_out, phase_1_p3, or_17_out);
  and MemWri (MemWri_out, phase_1_p3, or_18_out);
  and MemAcc (MemAcc_out, phase_1_p3, or_9_out);
  buf or_5 (or_5_out, instrdecode_1_out_17);  // OR_Gate
  Multiplexer #(.enable("false"), .select(2), .width(8)) multiplexer_6 (
    .in0(B), .in2(O), .in3({8{1'b0}}), .out(multiplexer_6_out), .sel(or_6_out));  // open: in1
  buf or_6 (or_6_out[0], or_14_out);  // OR_Gate
  or or_7 (or_6_out[1], or_10_out, or_14_out);
  or or_8 (or_8_out, instrdecode_1_out_14, instrdecode_1_out_13, instrdecode_1_out_12, instrdecode_1_out_8);
  Register8bit register8bit_3 (.out_5(B), .in_4(multiplexer_3_out), .Clk(Clk_out), .En(Bwrite_out), .Clr(Clr));
  or or_9 (or_9_out, or_18_out, or_19_out);
  or or_10 (or_10_out, instrdecode_1_out_14, instrdecode_1_out_13, instrdecode_1_out_12, instrdecode_1_out_9, instrdecode_1_out_8);
  buf or_11 (or_11_out, instrdecode_1_out_15);  // OR_Gate
  or or_12 (or_12_out[0], or_8_out, or_11_out);
  or or_13 (or_12_out[1], or_11_out, or_15_out);
  or or_14 (or_14_out, instrdecode_1_out_4, instrdecode_1_out_7, instrdecode_1_out_6, instrdecode_1_out_5, instrdecode_1_one);
  or or_15 (or_15_out, instrdecode_1_out_11, instrdecode_1_out_10, instrdecode_1_out_7, instrdecode_1_out_6, instrdecode_1_out_5, instrdecode_1_out_4, instrdecode_1_one);
  Register8bit register8bit_4 (.out_5(PC), .in_4(multiplexer_7_out), .Clk(Clk_out), .En(or_1_out), .Clr(Clr));
  Multiplexer #(.enable("false"), .width(8)) multiplexer_7 (
    .in0(adder8bit_3_q), .in1(multiplexer_3_out), .out(multiplexer_7_out), .sel(and_1_out));
  Adder8bit adder8bit_3 (.Q(adder8bit_3_q), .A(PC), .B(8'h1));  // open: C_out, C_in
  or or_16 (or_16_out, instrdecode_1_out_17, instrdecode_1_out_16, instrdecode_1_out_9, instrdecode_1_out_8, instrdecode_1_out_6, instrdecode_1_one);
  or or_17 (or_17_out, instrdecode_1_out_10, instrdecode_1_out_7, instrdecode_1_out_4);
  or or_18 (or_18_out, instrdecode_1_out_11, instrdecode_1_out_5);
  or or_19 (or_19_out, instrdecode_1_out_10, instrdecode_1_out_9, instrdecode_1_out_4, instrdecode_1_one);
  Register8bit register8bit_5 (.out_5(O), .in_4(multiplexer_8_out), .Clk(Clk_out), .En(or_20_out), .Clr(Clr));
  Multiplexer #(.enable("false"), .width(8)) multiplexer_8 (
    .in0({4'b0000, ram_1_dout_2}), .in1({O[3:0], ram_1_dout_2}), .out(multiplexer_8_out), .sel(and_3_out));
  or or_20 (or_20_out, phase_1_p1, and_3_out);
  InstrDecode instrdecode_1 (
    .out_6(instrdecode_1_out_6), .out_7(instrdecode_1_out_7), .out_8(instrdecode_1_out_8),
    .out_9(instrdecode_1_out_9), .out_10(instrdecode_1_out_10), .out_11(instrdecode_1_out_11),
    .out_12(instrdecode_1_out_12), .out_13(instrdecode_1_out_13), .out_14(instrdecode_1_out_14),
    .out_15(instrdecode_1_out_15), .out_16(instrdecode_1_out_16), .out_17(instrdecode_1_out_17),
    .out_18(instrdecode_1_out_18), .One(instrdecode_1_one), .out_4(instrdecode_1_out_4),
    .out_5(instrdecode_1_out_5), .OnOff(1'b1), .Instruction(multiplexer_9_out));
  and and_3 (and_3_out, phase_1_p1, instrdecode_1_out_18);
  Multiplexer #(.enable("false"), .width(4)) multiplexer_9 (
    .in0(out_4), .in1(in_2), .out(multiplexer_9_out), .sel(in_1));
  Phase phase_1 (.P1(phase_1_p1), .P2(phase_1_p2), .P3(phase_1_p3), .Clk(Clk_out), .Clr(Clr));
  Clock Clk (.out(Clk_out));

  assign out_5 = out_4;

  // Notes on the sheet:
  //   Phase2
  //   UncondBranch
  //   CondBranch
  //   Cpmarison
  //   Phase 3
  //   AwriteEn
  //   BwriteEn
  //   MemWrite
  //   MemAccess
  //   0to15
  //   Manual instruction
endmodule
