// Logisim project ComputerFinal.circ as structural Verilog: 1 circuit, main circuit DataPath
module DataPath (
  input  Clr,
  output [3:0] out_2,
  output [7:0] A,
  output [7:0] B,
  output [7:0] PC,
  output [7:0] O
);

  wire and_1_out, and_2_out, and_3_out, Awrite_out, Bwrite_out, Clk_out, demultiplexer_1_out0,
       demultiplexer_1_out1, demultiplexer_1_out2, demultiplexer_1_out3, demultiplexer_1_out4,
       demultiplexer_1_out5, demultiplexer_1_out6, demultiplexer_1_out7, demultiplexer_1_out8,
       demultiplexer_1_out9, demultiplexer_1_out10, demultiplexer_1_out11, demultiplexer_1_out12,
       demultiplexer_1_out13, demultiplexer_1_out14, demultiplexer_1_out15, logicunit_1_out_2,
       logicunit_1_out_3, MemAcc_out, MemWri_out, multiplexer_1_out, or_1_out, or_2_out, or_3_out, or_4_out,
       or_8_out, or_9_out, or_11_out, or_12_out, or_13_out, or_14_out, or_15_out, or_16_out, or_17_out,
       phase_1_p1, phase_1_p2, phase_1_p3;
  wire [1:0] or_6_out, or_10_out;
  wire [3:0] Opcode_out_5, ram_1_dout, ram_1_dout_2, undriven;
  wire [7:0] adder8bit_1_q, adder8bit_2_q, adder8bit_3_q, multiplexer_2_out, multiplexer_3_out,
       multiplexer_4_out, multiplexer_5_out, multiplexer_6_out, multiplexer_7_out, multiplexer_8_out,
       not_1_out, not_2_out;

  or or_1 (or_1_out, phase_1_p2, and_1_out);
  and and_1 (and_1_out, phase_1_p3, or_3_out);
  or or_2 (or_2_out, demultiplexer_1_out9, demultiplexer_1_out12);
  or or_3 (or_3_out, or_2_out, and_2_out);
  and and_2 (and_2_out, multiplexer_1_out, or_4_out);
  Multiplexer multiplexer_1 (
    .in0(logicunit_1_out_2), .in1(logicunit_1_out_3), .out(multiplexer_1_out), .sel(demultiplexer_1_out11));
  LogicUnit logicunit_1 (.out_3(logicunit_1_out_3), .out_2(logicunit_1_out_2), .in_1(adder8bit_1_q));
  Adder8bit adder8bit_1 (.Q(adder8bit_1_q), .A({8{1'b0}}), .B(not_1_out), .C_in(1'b1));  // open: C_out
  assign not_1_out = ~A;  // NOT_Gate not_1, 8 bits wide
  or or_4 (or_4_out, demultiplexer_1_out10, demultiplexer_1_out11);
  Register8bit Opcode (
    .out_5({out_2, Opcode_out_5}), .in_4({ram_1_dout, undriven}), .Clk(Clk_out), .En(phase_1_p1), .Clr(Clr));
  RAM #(.asyncread("true")) ram_1 (
    .addr(multiplexer_2_out), .we(MemWri_out), .oe(1'b1), .clk(Clk_out), .din(A),
    .dout({ram_1_dout, ram_1_dout_2}));
  Multiplexer #(.width(8)) multiplexer_2 (.in0(PC), .in1(adder8bit_2_q), .out(multiplexer_2_out), .sel(MemAcc_out));
  Adder8bit adder8bit_2 (
    .Q(adder8bit_2_q), .A(multiplexer_3_out), .B(multiplexer_5_out), .C_in(demultiplexer_1_out14));  // open: C_out
  Multiplexer #(.select(2), .width(8)) multiplexer_3 (
    .in0(A), .in1(PC), .in2(O), .in3({8{1'b0}}), .out(multiplexer_3_out), .sel(or_6_out));
  Register8bit A_reg (.out_5(A), .in_4(multiplexer_4_out), .Clk(Clk_out), .En(Awrite_out), .Clr(Clr));
  Multiplexer #(.width(8)) multiplexer_4 (
    .in0(adder8bit_2_q), .in1({ram_1_dout, ram_1_dout_2}), .out(multiplexer_4_out), .sel(MemAcc_out));
  Multiplexer #(.width(8)) multiplexer_5 (
    .in0(multiplexer_6_out), .in1(not_2_out), .out(multiplexer_5_out), .sel(demultiplexer_1_out14));
  assign not_2_out = ~multiplexer_6_out;  // NOT_Gate not_2, 8 bits wide
  and Awrite (Awrite_out, phase_1_p3, or_13_out);
  and Bwrite (Bwrite_out, phase_1_p3, or_14_out);
  and MemWri (MemWri_out, phase_1_p3, or_15_out);
  and MemAcc (MemAcc_out, phase_1_p3, or_8_out);
  Multiplexer #(.select(2), .width(8)) multiplexer_6 (
    .in0(B), .in2(O), .in3({8{1'b0}}), .out(multiplexer_6_out), .sel(or_10_out));  // open: in1
  or or_5 (or_10_out[1], or_9_out, or_10_out[0]);
  or or_6 (or_6_out[0], or_11_out, demultiplexer_1_out12);
  or or_7 (or_6_out[1], demultiplexer_1_out12, or_12_out);
  Register8bit B_reg (.out_5(B), .in_4(multiplexer_4_out), .Clk(Clk_out), .En(Bwrite_out), .Clr(Clr));
  or or_8 (or_8_out, or_15_out, or_16_out);
  or or_9 (or_9_out, demultiplexer_1_out11, demultiplexer_1_out10, demultiplexer_1_out9, demultiplexer_1_out6, demultiplexer_1_out5);
  or or_10 (or_10_out[0], demultiplexer_1_out4, demultiplexer_1_out3, demultiplexer_1_out2, demultiplexer_1_out1, demultiplexer_1_out0);
  or or_11 (or_11_out, demultiplexer_1_out11, demultiplexer_1_out10, demultiplexer_1_out9, demultiplexer_1_out5);
  or or_12 (or_12_out, demultiplexer_1_out8, demultiplexer_1_out7, demultiplexer_1_out4, demultiplexer_1_out3, demultiplexer_1_out2, demultiplexer_1_out1, demultiplexer_1_out0);
  Adder8bit adder8bit_3 (.Q(adder8bit_3_q), .A(PC), .B(8'h1));  // open: C_out, C_in
  Register8bit PC_reg (.out_5(PC), .in_4(multiplexer_7_out), .Clk(Clk_out), .En(or_1_out), .Clr(Clr));
  Multiplexer #(.width(8)) multiplexer_7 (
    .in0(adder8bit_3_q), .in1(multiplexer_4_out), .out(multiplexer_7_out), .sel(and_1_out));
  or or_13 (or_13_out, demultiplexer_1_out14, demultiplexer_1_out13, demultiplexer_1_out6, demultiplexer_1_out5, demultiplexer_1_out3, demultiplexer_1_out0);
  Register8bit Operand (.out_5(O), .in_4(multiplexer_8_out), .Clk(Clk_out), .En(or_17_out), .Clr(Clr));
  Multiplexer #(.width(8)) multiplexer_8 (
    .in0({4'b0000, ram_1_dout_2}), .in1({O[3:0], ram_1_dout_2}), .out(multiplexer_8_out), .sel(and_3_out));
  or or_14 (or_14_out, demultiplexer_1_out7, demultiplexer_1_out4, demultiplexer_1_out1);
  or or_15 (or_15_out, demultiplexer_1_out8, demultiplexer_1_out2);
  or or_16 (or_16_out, demultiplexer_1_out7, demultiplexer_1_out6, demultiplexer_1_out1, demultiplexer_1_out0);
  or or_17 (or_17_out, phase_1_p1, and_3_out);
  Demultiplexer #(.select(4)) demultiplexer_1 (
    .out0(demultiplexer_1_out0), .out1(demultiplexer_1_out1), .out2(demultiplexer_1_out2),
    .out3(demultiplexer_1_out3), .out4(demultiplexer_1_out4), .out5(demultiplexer_1_out5),
    .out6(demultiplexer_1_out6), .out7(demultiplexer_1_out7), .out8(demultiplexer_1_out8),
    .out9(demultiplexer_1_out9), .out10(demultiplexer_1_out10), .out11(demultiplexer_1_out11),
    .out12(demultiplexer_1_out12), .out13(demultiplexer_1_out13), .out14(demultiplexer_1_out14),
    .out15(demultiplexer_1_out15), .in(1'b1), .sel(out_2));
  and and_3 (and_3_out, phase_1_p1, demultiplexer_1_out15);
  Clock Clk (.out(Clk_out));
  Phase phase_1 (.P1(phase_1_p1), .P2(phase_1_p2), .P3(phase_1_p3), .Clk(Clk_out), .Clr(Clr));

  // Notes on the sheet:
  //   Phase2
  //   UncondBranch
  //   CondBranch
  //   Cpmarison
  //   Phase 3
  //   AwriteEn
  //   BwriteEn
  //   MemWrite
  //   MemAccess
  //   0to15
endmodule
