// Logisim project Data_path.circ as structural Verilog: 1 circuit, main circuit DataPath
module DataPath (
  input  Phase3,
  input  AwriteEn,
  input  BwriteEn,
  input  MemWrite,
  input  Phase2,
  input  UncondBranch,
  input  MemRead,
  input  CondBranch,
  input  OpWriteEn,
  input  Comparison,
  input  Sub,
  input  [1:0] in_12,
  input  [1:0] in_13,
  input  Clr,
  input  OwriteEn,
  input  Omode
);

  wire and_1_out, and_2_out, Awrite_out, Bwrite_out, Clk_out, logicunit_1_out_2, logicunit_1_out_3,
       MemAcc_out, MemWri_out, multiplexer_1_out, or_1_out, or_2_out, or_3_out;
  wire [3:0] main_1_out_6, main_1_out_6_2, undriven;
  wire [7:0] A_Reg_out_5, adder8bit_1_q, adder8bit_2_q, B_Reg_out_5, multiplexer_2_out, multiplexer_3_out,
       multiplexer_4_out, multiplexer_5_out, multiplexer_6_out, multiplexer_7_out, multiplexer_8_out,
       not_1_out, O_Reg_out_5, PC_Reg_out_5;

  or or_1 (or_1_out, Phase2, and_1_out);
  and and_1 (and_1_out, Phase3, or_2_out);
  or or_2 (or_2_out, UncondBranch, and_2_out);
  and and_2 (and_2_out, multiplexer_1_out, CondBranch);
  Multiplexer #(.enable("false")) multiplexer_1 (
    .in0(logicunit_1_out_2), .in1(logicunit_1_out_3), .out(multiplexer_1_out), .sel(Comparison));
  LogicUnit logicunit_1 (.out_3(logicunit_1_out_3), .out_2(logicunit_1_out_2), .in_1(A_Reg_out_5));
  Register8bit Opcode (.in_4({main_1_out_6_2, undriven}), .Clk(Clk_out), .En(OpWriteEn), .Clr(Clr));  // open: out_5
  Main main_1 (
    .out_6({main_1_out_6_2, main_1_out_6}), .W(MemWri_out), .Address(multiplexer_2_out), .Clr(Clr),
    .Clk(Clk_out));  // open: in_5
  Multiplexer #(.enable("false"), .width(8)) multiplexer_2 (
    .in0(PC_Reg_out_5), .in1(adder8bit_1_q), .out(multiplexer_2_out), .sel(MemAcc_out));
  Multiplexer #(.enable("false"), .width(8)) multiplexer_3 (
    .in0({main_1_out_6_2, main_1_out_6}), .in1(adder8bit_1_q), .out(multiplexer_3_out), .sel(MemAcc_out));
  Adder8bit adder8bit_1 (.Q(adder8bit_1_q), .A(multiplexer_4_out), .B(multiplexer_5_out), .C_in(Sub));  // open: C_out
  Multiplexer #(.enable("false"), .select(2), .width(8)) multiplexer_4 (
    .in0(A_Reg_out_5), .in1(PC_Reg_out_5), .in2(O_Reg_out_5), .out(multiplexer_4_out), .sel(in_12));  // open: in3
  Register8bit A_Reg (.out_5(A_Reg_out_5), .in_4(multiplexer_3_out), .Clk(Clk_out), .En(Awrite_out), .Clr(Clr));
  Multiplexer #(.enable("false"), .width(8)) multiplexer_5 (
    .in0(multiplexer_6_out), .in1(not_1_out), .out(multiplexer_5_out), .sel(Sub));
  assign not_1_out = ~multiplexer_6_out;  // NOT_Gate not_1, 8 bits wide
  and Awrite (Awrite_out, Phase3, AwriteEn);
  and Bwrite (Bwrite_out, Phase3, BwriteEn);
  and MemWri (MemWri_out, Phase3, MemWrite);
  and MemAcc (MemAcc_out, Phase3, or_3_out);
  or or_3 (or_3_out, MemWrite, MemRead);
  Multiplexer #(.enable("false"), .select(2), .width(8)) multiplexer_6 (
    .in0(B_Reg_out_5), .in2(O_Reg_out_5), .out(multiplexer_6_out), .sel(in_13));  // open: in1, in3
  Register8bit B_Reg (.out_5(B_Reg_out_5), .in_4(multiplexer_3_out), .Clk(Clk_out), .En(Bwrite_out), .Clr(Clr));
  Adder8bit adder8bit_2 (.Q(adder8bit_2_q), .A(PC_Reg_out_5), .B(8'h1));  // open: C_out, C_in
  Register8bit PC_Reg (.out_5(PC_Reg_out_5), .in_4(multiplexer_7_out), .Clk(Clk_out), .En(or_1_out), .Clr(Clr));
  Multiplexer #(.enable("false"), .width(8)) multiplexer_7 (
    .in0(adder8bit_2_q), .in1(multiplexer_3_out), .out(multiplexer_7_out), .sel(or_1_out));
  Register8bit O_Reg (.out_5(O_Reg_out_5), .in_4(multiplexer_8_out), .Clk(Clk_out), .En(OwriteEn), .Clr(Clr));
  Multiplexer #(.enable("false"), .width(4)) multiplexer_8 (
    .in0(main_1_out_6), .out(multiplexer_8_out[3:0]), .sel(Omode));  // open: in1
  Multiplexer #(.enable("false"), .width(4)) multiplexer_9 (
    .in1(O_Reg_out_5[7:4]), .out(multiplexer_8_out[7:4]), .sel(Omode));  // open: in0
  Clock Clk (.out(Clk_out));

  // Notes on the sheet:
  //   0: lower  1: upper
endmodule
