// Logisim project Half_adder.circ as structural Verilog: 1 circuit, main circuit main
module main (
  input  A,
  input  B,
  input  A_2,
  input  A_3,
  input  B_2,
  input  B_3,
  output Q,
  output Q_2,
  output Q_3,
  output Q_4,
  output Q_5,
  output Q_6
);

  wire nor_2_out, nor_3_out, nor_4_out, nor_6_out, nor_7_out, nor_8_out, nor_9_out, nor_11_out, nor_12_out,
       nor_13_out, not_1_out, not_2_out, not_3_out, not_4_out, not_7_out, not_8_out;

  not not_1 (not_1_out, A);
  not not_2 (not_2_out, B);
  not not_3 (not_3_out, A_2);
  not not_4 (not_4_out, B_2);
  nor nor_1 (Q, not_1_out, not_2_out);
  nor nor_2 (nor_2_out, A, B);
  nor nor_3 (nor_3_out, A, nor_2_out);
  nor nor_4 (nor_4_out, nor_2_out, B);
  nor nor_5 (Q_4, not_4_out, not_3_out);
  nor nor_6 (nor_6_out, nor_3_out, nor_4_out);
  nor nor_7 (nor_7_out, not_3_out, Q_4);
  nor nor_8 (nor_8_out, Q_4, not_4_out);
  not not_5 (Q_2, nor_6_out);
  nor nor_9 (nor_9_out, nor_7_out, nor_8_out);
  not not_6 (Q_6, nor_9_out);
  not not_7 (not_7_out, A_3);
  not not_8 (not_8_out, B_3);
  nor nor_10 (Q_3, not_7_out, not_8_out);
  nor nor_11 (nor_11_out, not_7_out, Q_3);
  nor nor_12 (nor_12_out, Q_3, not_8_out);
  nor nor_13 (nor_13_out, nor_11_out, nor_12_out);
  not not_9 (Q_5, nor_13_out);

  // Notes on the sheet:
  //   Inverting both inputs of the XOR gate doesn't change the output
  //   We use this to remove a NOR gate
endmodule
