// Logisim project Instruction_decoder.circ as structural Verilog: 1 circuit, main circuit InstrDecode
module InstrDecode (
  input  OnOff,
  input  [3:0] Instruction,
  output One,
  output out_4,
  output out_5,
  output out_6,
  output out_7,
  output out_8,
  output out_9,
  output out_10,
  output out_11,
  output out_12,
  output out_13,
  output out_14,
  output out_15,
  output out_16,
  output out_17,
  output out_18
);

  Demultiplexer #(.enable("false"), .select(4)) demultiplexer_1 (
    .out0(One), .out1(out_4), .out2(out_5), .out3(out_6), .out4(out_7), .out5(out_8), .out6(out_9),
    .out7(out_10), .out8(out_11), .out9(out_12), .out10(out_13), .out11(out_14), .out12(out_15),
    .out13(out_16), .out14(out_17), .out15(out_18), .in(OnOff), .sel(Instruction));
endmodule
