// Logisim project Logic_unit.circ as structural Verilog: 1 circuit, main circuit LogicUnit
module LogicUnit (
  input  [7:0] in_1,
  output out_2,
  output out_3
);

  wire or_1_out;

  or or_1 (or_1_out, in_1[0], in_1[1], in_1[2], in_1[3], in_1[4], in_1[5], in_1[6], in_1[7]);
  not not_1 (out_2, or_1_out);

  assign out_3 = in_1[7];
endmodule
