// Logisim project Multiplexer.circ as structural Verilog: 1 circuit, main circuit Multiplex
module Multiplex (
  input  [1:0] Select,
  input  [3:0] Inputs,
  output Output
);

  wire and_1_out, and_2_out, and_3_out, and_4_out, and_5_out, and_6_out, and_7_out, and_8_out, not_1_out,
       not_2_out, or_1_out, or_2_out;

  not not_1 (not_1_out, Select[0]);
  not not_2 (not_2_out, Select[1]);
  and and_1 (and_1_out, not_1_out, not_2_out);
  and and_2 (and_2_out, Select[0], not_2_out);
  and and_3 (and_3_out, not_1_out, Select[1]);
  and and_4 (and_4_out, Select[1], Select[0]);
  and and_5 (and_5_out, Inputs[0], and_1_out);
  and and_6 (and_6_out, Inputs[1], and_2_out);
  and and_7 (and_7_out, Inputs[2], and_3_out);
  and and_8 (and_8_out, Inputs[3], and_4_out);
  or or_1 (or_1_out, and_5_out, and_6_out);
  or or_2 (or_2_out, and_7_out, and_8_out);
  or or_3 (Output, or_1_out, or_2_out);

  // Notes on the sheet:
  //   Decode select signal
endmodule
