// Logisim project RAM.circ as structural Verilog: 7 circuits, main circuit MemoryBlock
module MemoryBlock (
  input  RdEn,
  input  Clr,
  input  D,
  input  Clk,
  input  WrEn,
  output Q
);

  wire nor_1_out, nor_2_out, nor_3_out, nor_4_out, nor_5_out, nor_6_out, nor_7_out, nor_8_out, nor_9_out,
       not_1_out, not_2_out, not_3_out, or_1_out, or_2_out, or_3_out, or_4_out;

  not not_1 (not_1_out, Clk);
  nor nor_1 (nor_1_out, not_1_out, WrEn);
  or or_1 (or_1_out, Clr, nor_1_out);
  not not_2 (not_2_out, D);
  nor nor_2 (nor_2_out, not_2_out, or_1_out);
  nor nor_3 (nor_3_out, or_1_out, D);
  nor nor_4 (nor_4_out, nor_2_out, nor_5_out);
  or or_2 (or_2_out, nor_4_out, Clr);
  nor nor_5 (nor_5_out, or_2_out, nor_3_out);
  not not_3 (not_3_out, or_1_out);
  or or_3 (or_3_out, Clr, not_3_out);
  nor nor_6 (nor_6_out, nor_5_out, or_3_out);
  nor nor_7 (nor_7_out, nor_4_out, or_3_out);
  or or_4 (or_4_out, Clr, nor_8_out);
  nor nor_8 (nor_8_out, nor_9_out, nor_7_out);
  nor nor_9 (nor_9_out, nor_6_out, or_4_out);
  nor nor_10 (Q, RdEn, nor_8_out);

  // Notes on the sheet:
  //   Negative logic for read and write
  //   Having read and write both powered (so off) makes it so you can't write to memory
endmodule

module MemoryByte (
  input  R,
  input  W,
  input  Clr,
  input  Clk,
  input  [7:0] in_5,
  input  [7:0] in_6,
  output [7:0] out_7
);

  wire [7:0] memoryblock_8_q;

  MemoryBlock memoryblock_1 (.Q(memoryblock_8_q[7]), .D(in_5[7]), .Clk(Clk), .WrEn(W), .RdEn(R), .Clr(Clr));
  MemoryBlock memoryblock_2 (.Q(memoryblock_8_q[6]), .D(in_5[6]), .Clk(Clk), .WrEn(W), .RdEn(R), .Clr(Clr));
  MemoryBlock memoryblock_3 (.Q(memoryblock_8_q[5]), .D(in_5[5]), .Clk(Clk), .WrEn(W), .RdEn(R), .Clr(Clr));
  MemoryBlock memoryblock_4 (.Q(memoryblock_8_q[4]), .D(in_5[4]), .Clk(Clk), .WrEn(W), .RdEn(R), .Clr(Clr));
  MemoryBlock memoryblock_5 (.Q(memoryblock_8_q[3]), .D(in_5[3]), .Clk(Clk), .WrEn(W), .RdEn(R), .Clr(Clr));
  MemoryBlock memoryblock_6 (.Q(memoryblock_8_q[2]), .D(in_5[2]), .Clk(Clk), .WrEn(W), .RdEn(R), .Clr(Clr));
  assign out_7 = memoryblock_8_q | in_6;  // OR_Gate or_1, 8 bits wide
  MemoryBlock memoryblock_7 (.Q(memoryblock_8_q[1]), .D(in_5[1]), .Clk(Clk), .WrEn(W), .RdEn(R), .Clr(Clr));
  MemoryBlock memoryblock_8 (.Q(memoryblock_8_q[0]), .D(in_5[0]), .Clk(Clk), .WrEn(W), .RdEn(R), .Clr(Clr));
endmodule

module Buff (
  input  [7:0] in_1,
  input  [7:0] in_2,
  output [7:0] out_3
);

  wire transistor_1_out, transistor_2_out, transistor_3_out, transistor_4_out, transistor_5_out,
       transistor_6_out, transistor_7_out, transistor_8_out;

  Transistor transistor_1 (.in(1'b1), .out(transistor_1_out), .gate(in_1[0]));
  Transistor transistor_2 (.in(1'b1), .out(transistor_2_out), .gate(in_1[1]));
  Transistor transistor_3 (.in(1'b1), .out(transistor_3_out), .gate(in_1[2]));
  Pull_Resistor pull_resistor_1 (.node(transistor_1_out));
  Pull_Resistor pull_resistor_2 (.node(transistor_2_out));
  Pull_Resistor pull_resistor_3 (.node(transistor_3_out));
  Transistor transistor_4 (.in(1'b1), .out(transistor_4_out), .gate(in_1[3]));
  Transistor transistor_5 (.in(1'b1), .out(transistor_5_out), .gate(in_1[4]));
  Transistor transistor_6 (.in(1'b1), .out(transistor_6_out), .gate(in_1[5]));
  Pull_Resistor pull_resistor_4 (.node(transistor_4_out));
  Pull_Resistor pull_resistor_5 (.node(transistor_5_out));
  Pull_Resistor pull_resistor_6 (.node(transistor_6_out));
  Transistor transistor_7 (.in(1'b1), .out(transistor_7_out), .gate(in_1[6]));
  Transistor transistor_8 (.in(1'b1), .out(transistor_8_out), .gate(in_1[7]));
  Pull_Resistor pull_resistor_7 (.node(transistor_7_out));
  Pull_Resistor pull_resistor_8 (.node(transistor_8_out));
  not not_1 (out_3[0], transistor_1_out);
  not not_2 (out_3[1], transistor_2_out);
  not not_3 (out_3[2], transistor_3_out);
  not not_4 (out_3[3], transistor_4_out);
  not not_5 (out_3[4], transistor_5_out);
  not not_6 (out_3[5], transistor_6_out);
  not not_7 (out_3[6], transistor_7_out);
  not not_8 (out_3[7], transistor_8_out);
  Transistor transistor_9 (.in(1'b1), .out(transistor_1_out), .gate(in_2[0]));
  Transistor transistor_10 (.in(1'b1), .out(transistor_2_out), .gate(in_2[1]));
  Transistor transistor_11 (.in(1'b1), .out(transistor_3_out), .gate(in_2[2]));
  Transistor transistor_12 (.in(1'b1), .out(transistor_4_out), .gate(in_2[3]));
  Transistor transistor_13 (.in(1'b1), .out(transistor_5_out), .gate(in_2[4]));
  Transistor transistor_14 (.in(1'b1), .out(transistor_6_out), .gate(in_2[5]));
  Transistor transistor_15 (.in(1'b1), .out(transistor_7_out), .gate(in_2[6]));
  Transistor transistor_16 (.in(1'b1), .out(transistor_8_out), .gate(in_2[7]));

  // Notes on the sheet:
  //   in_1: pull=down
  //   in_2: pull=down
  //   Inputs pull down so if they are disconnected, they are 0s.
endmodule

module Main (
  input  [7:0] Address,
  input  W,
  input  Clr,
  input  Clk,
  input  [7:0] in_5,
  output [7:0] out_6
);

  wire or_3_out, or_4_out, or_5_out, or_6_out, or_7_out, or_8_out, or_9_out, or_10_out, or_11_out, or_12_out,
       or_13_out, or_14_out, or_15_out, or_16_out, or_17_out, or_18_out, or_19_out, or_20_out, or_21_out,
       or_22_out, or_23_out, or_24_out, or_25_out, or_26_out, or_27_out, or_28_out, or_29_out, or_30_out,
       or_31_out, or_32_out, or_33_out, or_34_out, or_35_out, or_36_out, or_37_out, or_38_out, or_39_out,
       or_40_out, or_41_out, or_42_out, or_43_out, or_44_out, or_45_out, or_46_out, or_47_out, or_48_out,
       or_49_out, or_50_out, or_51_out, or_52_out, or_53_out, or_54_out, or_55_out, or_56_out, or_57_out,
       or_58_out, or_59_out, or_60_out, or_61_out, or_62_out, or_63_out, or_64_out, or_65_out, or_66_out;
  wire [7:0] decode_1_out_2, decode_2_out_2, memorybyte_1_out_7, memorybyte_2_out_7, memorybyte_3_out_7,
       memorybyte_4_out_7, memorybyte_5_out_7, memorybyte_6_out_7, memorybyte_7_out_7, memorybyte_8_out_7,
       memorybyte_9_out_7, memorybyte_10_out_7, memorybyte_11_out_7, memorybyte_12_out_7,
       memorybyte_13_out_7, memorybyte_14_out_7, memorybyte_15_out_7, memorybyte_16_out_7,
       memorybyte_17_out_7, memorybyte_18_out_7, memorybyte_19_out_7, memorybyte_20_out_7,
       memorybyte_21_out_7, memorybyte_22_out_7, memorybyte_23_out_7, memorybyte_24_out_7,
       memorybyte_25_out_7, memorybyte_26_out_7, memorybyte_27_out_7, memorybyte_28_out_7,
       memorybyte_29_out_7, memorybyte_30_out_7, memorybyte_31_out_7, memorybyte_32_out_7, or_1_out,
       or_2_out, or_68_out, or_69_out;
  wire [7:7] not_1_out;

  assign or_1_out = decode_2_out_2 | {8{not_1_out[7]}};  // OR_Gate or_1, 8 bits wide
  not not_1 (not_1_out[7], W);
  Decode decode_1 (.out_2(decode_1_out_2), .in_1(Address[2:0]));
  Decode decode_2 (.out_2(decode_2_out_2), .in_1({1'b0, Address[4:3]}));
  assign or_2_out = decode_1_out_2 | {8{not_1_out[7]}};  // OR_Gate or_2, 8 bits wide
  or or_3 (or_3_out, decode_2_out_2[0], decode_1_out_2[0]);
  or or_4 (or_4_out, or_1_out[0], or_2_out[0]);
  MemoryByte memorybyte_1 (
    .out_7(memorybyte_1_out_7), .W(or_4_out), .Clr(Clr), .Clk(Clk), .in_5(in_5), .in_6({8{1'b0}}),
    .R(or_3_out));
  or or_5 (or_5_out, decode_2_out_2[1], decode_1_out_2[0]);
  or or_6 (or_6_out, or_1_out[1], or_2_out[0]);
  MemoryByte memorybyte_2 (
    .out_7(memorybyte_2_out_7), .W(or_6_out), .Clr(Clr), .Clk(Clk), .in_5(in_5), .in_6({8{1'b0}}),
    .R(or_5_out));
  or or_7 (or_7_out, decode_2_out_2[2], decode_1_out_2[0]);
  or or_8 (or_8_out, or_1_out[2], or_2_out[0]);
  MemoryByte memorybyte_3 (
    .out_7(memorybyte_3_out_7), .W(or_8_out), .Clr(Clr), .Clk(Clk), .in_5(in_5), .in_6({8{1'b0}}),
    .R(or_7_out));
  or or_9 (or_9_out, decode_2_out_2[3], decode_1_out_2[0]);
  or or_10 (or_10_out, or_1_out[3], or_2_out[0]);
  MemoryByte memorybyte_4 (
    .out_7(memorybyte_4_out_7), .W(or_10_out), .Clr(Clr), .Clk(Clk), .in_5(in_5), .in_6({8{1'b0}}),
    .R(or_9_out));
  or or_11 (or_11_out, decode_2_out_2[0], decode_1_out_2[1]);
  or or_12 (or_12_out, or_1_out[0], or_2_out[1]);
  MemoryByte memorybyte_5 (
    .out_7(memorybyte_5_out_7), .W(or_12_out), .Clr(Clr), .Clk(Clk), .in_5(in_5), .in_6(memorybyte_1_out_7),
    .R(or_11_out));
  or or_13 (or_13_out, decode_2_out_2[1], decode_1_out_2[1]);
  or or_14 (or_14_out, or_1_out[1], or_2_out[1]);
  MemoryByte memorybyte_6 (
    .out_7(memorybyte_6_out_7), .W(or_14_out), .Clr(Clr), .Clk(Clk), .in_5(in_5), .in_6(memorybyte_2_out_7),
    .R(or_13_out));
  or or_15 (or_15_out, decode_2_out_2[2], decode_1_out_2[1]);
  or or_16 (or_16_out, or_1_out[2], or_2_out[1]);
  MemoryByte memorybyte_7 (
    .out_7(memorybyte_7_out_7), .W(or_16_out), .Clr(Clr), .Clk(Clk), .in_5(in_5), .in_6(memorybyte_3_out_7),
    .R(or_15_out));
  or or_17 (or_17_out, decode_2_out_2[3], decode_1_out_2[1]);
  or or_18 (or_18_out, or_1_out[3], or_2_out[1]);
  MemoryByte memorybyte_8 (
    .out_7(memorybyte_8_out_7), .W(or_18_out), .Clr(Clr), .Clk(Clk), .in_5(in_5), .in_6(memorybyte_4_out_7),
    .R(or_17_out));
  or or_19 (or_19_out, decode_2_out_2[0], decode_1_out_2[2]);
  or or_20 (or_20_out, decode_2_out_2[1], decode_1_out_2[2]);
  or or_21 (or_21_out, decode_2_out_2[2], decode_1_out_2[2]);
  or or_22 (or_22_out, decode_2_out_2[3], decode_1_out_2[2]);
  or or_23 (or_23_out, or_1_out[0], or_2_out[2]);
  MemoryByte memorybyte_9 (
    .out_7(memorybyte_9_out_7), .W(or_23_out), .Clr(Clr), .Clk(Clk), .in_5(in_5), .in_6(memorybyte_5_out_7),
    .R(or_19_out));
  or or_24 (or_24_out, or_1_out[1], or_2_out[2]);
  MemoryByte memorybyte_10 (
    .out_7(memorybyte_10_out_7), .W(or_24_out), .Clr(Clr), .Clk(Clk), .in_5(in_5), .in_6(memorybyte_6_out_7),
    .R(or_20_out));
  or or_25 (or_25_out, or_1_out[2], or_2_out[2]);
  MemoryByte memorybyte_11 (
    .out_7(memorybyte_11_out_7), .W(or_25_out), .Clr(Clr), .Clk(Clk), .in_5(in_5), .in_6(memorybyte_7_out_7),
    .R(or_21_out));
  or or_26 (or_26_out, or_1_out[3], or_2_out[2]);
  MemoryByte memorybyte_12 (
    .out_7(memorybyte_12_out_7), .W(or_26_out), .Clr(Clr), .Clk(Clk), .in_5(in_5), .in_6(memorybyte_8_out_7),
    .R(or_22_out));
  or or_27 (or_27_out, decode_2_out_2[0], decode_1_out_2[3]);
  or or_28 (or_28_out, or_1_out[0], or_2_out[3]);
  MemoryByte memorybyte_13 (
    .out_7(memorybyte_13_out_7), .W(or_28_out), .Clr(Clr), .Clk(Clk), .in_5(in_5), .in_6(memorybyte_9_out_7),
    .R(or_27_out));
  or or_29 (or_29_out, decode_2_out_2[1], decode_1_out_2[3]);
  or or_30 (or_30_out, or_1_out[1], or_2_out[3]);
  MemoryByte memorybyte_14 (
    .out_7(memorybyte_14_out_7), .W(or_30_out), .Clr(Clr), .Clk(Clk), .in_5(in_5),
    .in_6(memorybyte_10_out_7), .R(or_29_out));
  or or_31 (or_31_out, decode_2_out_2[2], decode_1_out_2[3]);
  or or_32 (or_32_out, or_1_out[2], or_2_out[3]);
  MemoryByte memorybyte_15 (
    .out_7(memorybyte_15_out_7), .W(or_32_out), .Clr(Clr), .Clk(Clk), .in_5(in_5),
    .in_6(memorybyte_11_out_7), .R(or_31_out));
  or or_33 (or_33_out, decode_2_out_2[3], decode_1_out_2[3]);
  or or_34 (or_34_out, or_1_out[3], or_2_out[3]);
  MemoryByte memorybyte_16 (
    .out_7(memorybyte_16_out_7), .W(or_34_out), .Clr(Clr), .Clk(Clk), .in_5(in_5),
    .in_6(memorybyte_12_out_7), .R(or_33_out));
  or or_35 (or_35_out, decode_2_out_2[0], decode_1_out_2[4]);
  or or_36 (or_36_out, or_1_out[0], or_2_out[4]);
  or or_37 (or_37_out, decode_2_out_2[1], decode_1_out_2[4]);
  or or_38 (or_38_out, or_1_out[1], or_2_out[4]);
  or or_39 (or_39_out, decode_2_out_2[2], decode_1_out_2[4]);
  or or_40 (or_40_out, or_1_out[2], or_2_out[4]);
  or or_41 (or_41_out, decode_2_out_2[3], decode_1_out_2[4]);
  or or_42 (or_42_out, or_1_out[3], or_2_out[4]);
  or or_43 (or_43_out, decode_2_out_2[0], decode_1_out_2[5]);
  MemoryByte memorybyte_17 (
    .out_7(memorybyte_17_out_7), .W(or_36_out), .Clr(Clr), .Clk(Clk), .in_5(in_5),
    .in_6(memorybyte_13_out_7), .R(or_35_out));
  or or_44 (or_44_out, decode_2_out_2[1], decode_1_out_2[5]);
  MemoryByte memorybyte_18 (
    .out_7(memorybyte_18_out_7), .W(or_38_out), .Clr(Clr), .Clk(Clk), .in_5(in_5),
    .in_6(memorybyte_14_out_7), .R(or_37_out));
  or or_45 (or_45_out, decode_2_out_2[2], decode_1_out_2[5]);
  MemoryByte memorybyte_19 (
    .out_7(memorybyte_19_out_7), .W(or_40_out), .Clr(Clr), .Clk(Clk), .in_5(in_5),
    .in_6(memorybyte_15_out_7), .R(or_39_out));
  or or_46 (or_46_out, decode_2_out_2[3], decode_1_out_2[5]);
  MemoryByte memorybyte_20 (
    .out_7(memorybyte_20_out_7), .W(or_42_out), .Clr(Clr), .Clk(Clk), .in_5(in_5),
    .in_6(memorybyte_16_out_7), .R(or_41_out));
  or or_47 (or_47_out, or_1_out[0], or_2_out[5]);
  MemoryByte memorybyte_21 (
    .out_7(memorybyte_21_out_7), .W(or_47_out), .Clr(Clr), .Clk(Clk), .in_5(in_5),
    .in_6(memorybyte_17_out_7), .R(or_43_out));
  or or_48 (or_48_out, or_1_out[1], or_2_out[5]);
  MemoryByte memorybyte_22 (
    .out_7(memorybyte_22_out_7), .W(or_48_out), .Clr(Clr), .Clk(Clk), .in_5(in_5),
    .in_6(memorybyte_18_out_7), .R(or_44_out));
  or or_49 (or_49_out, or_1_out[2], or_2_out[5]);
  MemoryByte memorybyte_23 (
    .out_7(memorybyte_23_out_7), .W(or_49_out), .Clr(Clr), .Clk(Clk), .in_5(in_5),
    .in_6(memorybyte_19_out_7), .R(or_45_out));
  or or_50 (or_50_out, or_1_out[3], or_2_out[5]);
  MemoryByte memorybyte_24 (
    .out_7(memorybyte_24_out_7), .W(or_50_out), .Clr(Clr), .Clk(Clk), .in_5(in_5),
    .in_6(memorybyte_20_out_7), .R(or_46_out));
  or or_51 (or_51_out, decode_2_out_2[0], decode_1_out_2[6]);
  or or_52 (or_52_out, or_1_out[0], or_2_out[6]);
  MemoryByte memorybyte_25 (
    .out_7(memorybyte_25_out_7), .W(or_52_out), .Clr(Clr), .Clk(Clk), .in_5(in_5),
    .in_6(memorybyte_21_out_7), .R(or_51_out));
  or or_53 (or_53_out, decode_2_out_2[1], decode_1_out_2[6]);
  or or_54 (or_54_out, or_1_out[1], or_2_out[6]);
  MemoryByte memorybyte_26 (
    .out_7(memorybyte_26_out_7), .W(or_54_out), .Clr(Clr), .Clk(Clk), .in_5(in_5),
    .in_6(memorybyte_22_out_7), .R(or_53_out));
  or or_55 (or_55_out, decode_2_out_2[2], decode_1_out_2[6]);
  or or_56 (or_56_out, or_1_out[2], or_2_out[6]);
  MemoryByte memorybyte_27 (
    .out_7(memorybyte_27_out_7), .W(or_56_out), .Clr(Clr), .Clk(Clk), .in_5(in_5),
    .in_6(memorybyte_23_out_7), .R(or_55_out));
  or or_57 (or_57_out, decode_2_out_2[3], decode_1_out_2[6]);
  or or_58 (or_58_out, or_1_out[3], or_2_out[6]);
  MemoryByte memorybyte_28 (
    .out_7(memorybyte_28_out_7), .W(or_58_out), .Clr(Clr), .Clk(Clk), .in_5(in_5),
    .in_6(memorybyte_24_out_7), .R(or_57_out));
  or or_59 (or_59_out, decode_2_out_2[0], decode_1_out_2[7]);
  or or_60 (or_60_out, or_1_out[0], or_2_out[7]);
  or or_61 (or_61_out, decode_2_out_2[1], decode_1_out_2[7]);
  or or_62 (or_62_out, or_1_out[1], or_2_out[7]);
  or or_63 (or_63_out, decode_2_out_2[2], decode_1_out_2[7]);
  or or_64 (or_64_out, or_1_out[2], or_2_out[7]);
  or or_65 (or_65_out, decode_2_out_2[3], decode_1_out_2[7]);
  or or_66 (or_66_out, or_1_out[3], or_2_out[7]);
  MemoryByte memorybyte_29 (
    .out_7(memorybyte_29_out_7), .W(or_60_out), .Clr(Clr), .Clk(Clk), .in_5(in_5),
    .in_6(memorybyte_25_out_7), .R(or_59_out));
  MemoryByte memorybyte_30 (
    .out_7(memorybyte_30_out_7), .W(or_62_out), .Clr(Clr), .Clk(Clk), .in_5(in_5),
    .in_6(memorybyte_26_out_7), .R(or_61_out));
  MemoryByte memorybyte_31 (
    .out_7(memorybyte_31_out_7), .W(or_64_out), .Clr(Clr), .Clk(Clk), .in_5(in_5),
    .in_6(memorybyte_27_out_7), .R(or_63_out));
  MemoryByte memorybyte_32 (
    .out_7(memorybyte_32_out_7), .W(or_66_out), .Clr(Clr), .Clk(Clk), .in_5(in_5),
    .in_6(memorybyte_28_out_7), .R(or_65_out));
  assign out_6 = memorybyte_29_out_7 | or_68_out;  // OR_Gate or_67, 8 bits wide
  assign or_68_out = memorybyte_30_out_7 | or_69_out;  // OR_Gate or_68, 8 bits wide
  assign or_69_out = memorybyte_31_out_7 | memorybyte_32_out_7;  // OR_Gate or_69, 8 bits wide

  // Notes on the sheet:
  //   2-to-4 decoder
  //   from a 3-to-8 decoder
  //   We optimise the circuit by noticing that MemBlock uses MemCell
  //   and MemCell would otherwise contain inverters on the R/W inputs
  //   and the OR gates in the grid would usually be NOR gates.
  //   The double inversion can be eliminated.
  //   Inside this memory there's negative logic going on.
endmodule

module Decode (
  input  [2:0] in_1,
  output [7:0] out_2
);

  wire not_1_out, not_2_out, not_3_out;

  not not_1 (not_1_out, in_1[0]);
  not not_2 (not_2_out, in_1[1]);
  not not_3 (not_3_out, in_1[2]);
  or or_1 (out_2[0], in_1[0], in_1[1], in_1[2]);
  or or_2 (out_2[1], not_1_out, in_1[1], in_1[2]);
  or or_3 (out_2[2], in_1[0], not_2_out, in_1[2]);
  or or_4 (out_2[3], not_1_out, not_2_out, in_1[2]);
  or or_5 (out_2[4], in_1[0], in_1[1], not_3_out);
  or or_6 (out_2[5], not_1_out, in_1[1], not_3_out);
  or or_7 (out_2[6], in_1[0], not_2_out, not_3_out);
  or or_8 (out_2[7], not_1_out, not_2_out, not_3_out);

  // Notes on the sheet:
  //   Minecraft can support OR gates with more than 2 inputs
  //   We turn this into an active-low decoder for the sake of the memory usage
endmodule

module Bufftest (
  input  [7:0] in_1,
  input  [7:0] in_2,
  output [7:0] out_3
);

  Transistor #(.\type ("n")) transistor_1 (.in(1'b1), .out(out_3[0]), .gate(in_1[0]));
  Transistor #(.\type ("n")) transistor_2 (.in(1'b1), .out(out_3[1]), .gate(in_1[1]));
  Transistor #(.\type ("n")) transistor_3 (.in(1'b1), .out(out_3[2]), .gate(in_1[2]));
  Pull_Resistor pull_resistor_1 (.node(out_3[0]));
  Pull_Resistor pull_resistor_2 (.node(out_3[1]));
  Pull_Resistor pull_resistor_3 (.node(out_3[2]));
  Transistor #(.\type ("n")) transistor_4 (.in(1'b1), .out(out_3[3]), .gate(in_1[3]));
  Transistor #(.\type ("n")) transistor_5 (.in(1'b1), .out(out_3[4]), .gate(in_1[4]));
  Transistor #(.\type ("n")) transistor_6 (.in(1'b1), .out(out_3[5]), .gate(in_1[5]));
  Pull_Resistor pull_resistor_4 (.node(out_3[3]));
  Pull_Resistor pull_resistor_5 (.node(out_3[4]));
  Pull_Resistor pull_resistor_6 (.node(out_3[5]));
  Transistor #(.\type ("n")) transistor_7 (.in(1'b1), .out(out_3[6]), .gate(in_1[6]));
  Transistor #(.\type ("n")) transistor_8 (.in(1'b1), .out(out_3[7]), .gate(in_1[7]));
  Pull_Resistor pull_resistor_7 (.node(out_3[6]));
  Pull_Resistor pull_resistor_8 (.node(out_3[7]));
  Transistor #(.\type ("n")) transistor_9 (.in(1'b1), .out(out_3[0]), .gate(in_2[0]));
  Transistor #(.\type ("n")) transistor_10 (.in(1'b1), .out(out_3[1]), .gate(in_2[1]));
  Transistor #(.\type ("n")) transistor_11 (.in(1'b1), .out(out_3[2]), .gate(in_2[2]));
  Transistor #(.\type ("n")) transistor_12 (.in(1'b1), .out(out_3[3]), .gate(in_2[3]));
  Transistor #(.\type ("n")) transistor_13 (.in(1'b1), .out(out_3[4]), .gate(in_2[4]));
  Transistor #(.\type ("n")) transistor_14 (.in(1'b1), .out(out_3[5]), .gate(in_2[5]));
  Transistor #(.\type ("n")) transistor_15 (.in(1'b1), .out(out_3[6]), .gate(in_2[6]));
  Transistor #(.\type ("n")) transistor_16 (.in(1'b1), .out(out_3[7]), .gate(in_2[7]));

  // Notes on the sheet:
  //   in_1: pull=down
  //   in_2: pull=down
  //   Inputs pull down so if they are disconnected, they are 0s.
endmodule

module Bufftest2 (
  input  [7:0] A,
  input  [7:0] B,
  output [7:0] Q
);

  assign Q = A | B;  // OR_Gate or_1, 8 bits wide
endmodule
