// Logisim project Register.circ as structural Verilog: 7 circuits, main circuit SRlatch
module SRlatch (
  input  Reset,
  input  Set,
  output Q,
  output Qprime
);

  nor nor_1 (Q, Reset, Qprime);
  nor nor_2 (Qprime, Q, Set);
endmodule

module ClockGatedSRlatch (
  input  R,
  input  Clk,
  input  S,
  output Q,
  output Qprime
);

  wire and_1_out, and_2_out;

  and and_1 (and_1_out, R, Clk);
  and and_2 (and_2_out, Clk, S);
  SRlatch srlatch_1 (.Q(Q), .Qprime(Qprime), .Set(and_2_out), .Reset(and_1_out));

  // Notes on the sheet:
  //   SR latch only changes value when the clock signal is on
endmodule

module DataLatch1 (
  input  Clk,
  input  D,
  output Q,
  output Qprime
);

  wire not_1_out;

  not not_1 (not_1_out, D);
  ClockGatedSRlatch clockgatedsrlatch_1 (.Q(Q), .Qprime(Qprime), .Clk(Clk), .S(D), .R(not_1_out));

  // Notes on the sheet:
  //   Whenever the clock is high the value on the data input is stored into the data latch
endmodule

module DataFlipFlop (
  input  D,
  input  Clk,
  output Q,
  output Qprime
);

  wire datalatch1_1_q, not_1_out;

  DataLatch1 datalatch1_1 (.Q(datalatch1_1_q), .Clk(Clk), .D(D));  // open: Qprime
  DataLatch1 datalatch1_2 (.Q(Q), .Qprime(Qprime), .Clk(not_1_out), .D(datalatch1_1_q));
  not not_1 (not_1_out, Clk);

  // Notes on the sheet:
  //   Negative-edge triggered D-flip-flop
  //   Remove NOT gate for positive-edge triggered D-flip-flop
endmodule

module DataLatch2 (
  input  D,
  input  Enable,
  input  Clk,
  output Q,
  output Qprime
);

  wire and_1_out, not_1_out;

  not not_1 (not_1_out, D);
  and and_1 (and_1_out, Enable, Clk);
  ClockGatedSRlatch clockgatedsrlatch_1 (.Q(Q), .Qprime(Qprime), .Clk(and_1_out), .S(D), .R(not_1_out));
endmodule

module DTypeMasterSlaveFlipFlop (
  input  Clr,
  input  D,
  input  Clk,
  input  En,
  output Q,
  output out_6
);

  wire nor_1_out, nor_2_out, nor_3_out, nor_4_out, nor_5_out, nor_6_out, nor_7_out, not_1_out, not_2_out,
       not_3_out, not_4_out, or_1_out, or_2_out, or_3_out, or_4_out;

  not not_1 (not_1_out, Clk);
  not not_2 (not_2_out, En);
  nor nor_1 (nor_1_out, not_1_out, not_2_out);
  or or_1 (or_1_out, Clr, nor_1_out);
  not not_3 (not_3_out, D);
  nor nor_2 (nor_2_out, not_3_out, or_1_out);
  nor nor_3 (nor_3_out, or_1_out, D);
  nor nor_4 (nor_4_out, nor_2_out, nor_5_out);
  or or_2 (or_2_out, nor_4_out, Clr);
  nor nor_5 (nor_5_out, or_2_out, nor_3_out);
  not not_4 (not_4_out, or_1_out);
  or or_3 (or_3_out, Clr, not_4_out);
  nor nor_6 (nor_6_out, nor_5_out, or_3_out);
  nor nor_7 (nor_7_out, nor_4_out, or_3_out);
  or or_4 (or_4_out, Clr, out_6);
  nor nor_8 (out_6, Q, nor_7_out);
  nor nor_9 (Q, nor_6_out, or_4_out);

  // Notes on the sheet:
  //   May want to remove not gate to make positive edge the default
  //   Reset is synchronous: it only work when the clock is toggled
  //   When enable is on the stored value changes on the positive clock edge
  //   Asynchronous means the clock signal is set to zero whenever the clear signal is high, regardless of the clock
endmodule

module Register8bit (
  input  Clk,
  input  En,
  input  Clr,
  input  [7:0] in_4,
  output [7:0] out_5
);

  DTypeMasterSlaveFlipFlop dtypemasterslaveflipflop_1 (
    .Q(out_5[0]), .D(in_4[0]), .Clk(Clk), .En(En), .Clr(Clr));  // open: out_6
  DTypeMasterSlaveFlipFlop dtypemasterslaveflipflop_2 (
    .Q(out_5[1]), .D(in_4[1]), .Clk(Clk), .En(En), .Clr(Clr));  // open: out_6
  DTypeMasterSlaveFlipFlop dtypemasterslaveflipflop_3 (
    .Q(out_5[2]), .D(in_4[2]), .Clk(Clk), .En(En), .Clr(Clr));  // open: out_6
  DTypeMasterSlaveFlipFlop dtypemasterslaveflipflop_4 (
    .Q(out_5[3]), .D(in_4[3]), .Clk(Clk), .En(En), .Clr(Clr));  // open: out_6
  DTypeMasterSlaveFlipFlop dtypemasterslaveflipflop_5 (
    .Q(out_5[4]), .D(in_4[4]), .Clk(Clk), .En(En), .Clr(Clr));  // open: out_6
  DTypeMasterSlaveFlipFlop dtypemasterslaveflipflop_6 (
    .Q(out_5[5]), .D(in_4[5]), .Clk(Clk), .En(En), .Clr(Clr));  // open: out_6
  DTypeMasterSlaveFlipFlop dtypemasterslaveflipflop_7 (
    .Q(out_5[6]), .D(in_4[6]), .Clk(Clk), .En(En), .Clr(Clr));  // open: out_6
  DTypeMasterSlaveFlipFlop dtypemasterslaveflipflop_8 (
    .Q(out_5[7]), .D(in_4[7]), .Clk(Clk), .En(En), .Clr(Clr));  // open: out_6
endmodule
