// Logisim project SR_latch.circ as structural Verilog: 2 circuits, main circuit SRlatch
module SRlatch (
  input  Reset,
  input  Set,
  output Q,
  output Qprime
);

  nor nor_1 (Q, Reset, Qprime);
  nor nor_2 (Qprime, Q, Set);
endmodule

module ClockGatedSRlatch (
  input  R,
  input  Clk,
  input  S,
  output Q,
  output Qprime
);

  wire and_1_out, and_2_out;

  and and_1 (and_1_out, R, Clk);
  and and_2 (and_2_out, Clk, S);
  SRlatch srlatch_1 (.Reset(and_1_out), .Set(and_2_out), .Q(Q), .Qprime(Qprime));

  // Notes on the sheet:
  //   SR latch only changes value when the clock signal is on
endmodule
